# Fritzing sketch MeshMasterWebServer-OLED (saved by Fritzing 1.0.1rc)

parts:
  MH-ET_LIVE_ESP32_DEVKIT5 = MH-ET LIVE ESP32 DEVKIT 38 pins
  MH-ET_LIVE_ESP32_DEVKIT6 = MH-ET LIVE ESP32 DEVKIT 38 pins
  Bauteil5 = OLED Monochrome 128x32 I2C [part_number=931]
  Bauteil6 = OLED Monochrome 128x32 I2C [part_number=931]

nets:
  3V3: MH-ET_LIVE_ESP32_DEVKIT5.3V3, Bauteil5.3.3V
  GND: MH-ET_LIVE_ESP32_DEVKIT5.GND, Bauteil5.GND
  N1: MH-ET_LIVE_ESP32_DEVKIT5.IO22, Bauteil5.SCL
  N2: MH-ET_LIVE_ESP32_DEVKIT5.IO21, Bauteil5.SDA
  N3: MH-ET_LIVE_ESP32_DEVKIT5.IO17, MH-ET_LIVE_ESP32_DEVKIT6.IO16
  N4: MH-ET_LIVE_ESP32_DEVKIT5.IO16, MH-ET_LIVE_ESP32_DEVKIT6.IO17
  3V3_2: MH-ET_LIVE_ESP32_DEVKIT6.3V3, Bauteil6.3.3V
  GND_2: MH-ET_LIVE_ESP32_DEVKIT6.GND, Bauteil6.GND
  N5: MH-ET_LIVE_ESP32_DEVKIT6.IO22, Bauteil6.SCL
  N6: MH-ET_LIVE_ESP32_DEVKIT6.IO21, Bauteil6.SDA

notes:
  WebServer
  MeshMaster

custom parts:
  MH-ET LIVE ESP32 DEVKIT 38 pins: http://mh.nodebb.com/topic/2/mh-et-live-esp32-devkit
  OLED Monochrome 128x32 I2C: These displays are small, only about 1" diagonal, but very readable due to the high contrast of an OLED display. This display is made of 128x32 individual white OLED pixels, each one is turned on or off by the controller chip. Because the display makes its own light, no backlight is required. This reduces the power required to run the OLED and is why the display has such high contrast; we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
