# Fritzing sketch MeshNodeSensors (saved by Fritzing 1.0.2b)

parts:
  MH-ET_LIVE_ESP32_DEVKIT1 = MH-ET LIVE ESP32 DEVKIT 38 pins
  Grove1 = Grove OLED 128x96
  DHT1 = DHT11 Humitidy and Temperature Sensor (3 pins)
  Bauteil3 = HX711 Weighing Sensor Module

nets:
  VCC: MH-ET_LIVE_ESP32_DEVKIT1.3V3, Grove1.VCC, DHT1.Plus, Bauteil3.VCC
  N1: MH-ET_LIVE_ESP32_DEVKIT1.GND#64, Grove1.GND
  N2: MH-ET_LIVE_ESP32_DEVKIT1.IO22, Grove1.SCL
  N3: MH-ET_LIVE_ESP32_DEVKIT1.IO21, Grove1.SDA
  GND: MH-ET_LIVE_ESP32_DEVKIT1.GND#70, DHT1.Gnd, Bauteil3.GND
  N4: MH-ET_LIVE_ESP32_DEVKIT1.IO16, Bauteil3.DO/RX
  N5: MH-ET_LIVE_ESP32_DEVKIT1.IO4, Bauteil3.CK/TX
  N6: MH-ET_LIVE_ESP32_DEVKIT1.IO15, DHT1.Signal

custom parts:
  MH-ET LIVE ESP32 DEVKIT 38 pins: http://mh.nodebb.com/topic/2/mh-et-live-esp32-devkit
  DHT11 Humitidy and Temperature Sensor (3 pins): DHT11 Humidity and Temperature Sensor (3 pins).
